// Logisim project 3.1_Comp4.circ as structural Verilog: 4 circuits, main circuit main
module main (
  output out_1,
  output out_2,
  output out_3,
  output out_4,
  output out_5,
  output out_6
);

  wire [3:0] slider_1_out, slider_2_out;

  Slider #(.width(4), .value('he)) slider_1 (.out(slider_1_out));
  Slider #(.width(4), .value('hb)) slider_2 (.out(slider_2_out));
  // Probe on slider_2_out
  // Probe on slider_1_out
  Comp4nat comp4nat_1 (.A_B_3(out_3), .A_B_2(out_2), .A_B(out_1), .A(slider_2_out), .B(slider_1_out));
  // Probe on slider_2_out
  // Probe on slider_1_out
  Comp4ent comp4ent_1 (.A_B_3(out_6), .A_B_2(out_5), .A_B(out_4), .A(slider_2_out), .B(slider_1_out));

  // Notes on the sheet:
  //   PractFC3.1 Equip XI13$Eric García Castro$Iván Molinero Moreno
endmodule

module Comp1bit (
  input  a,
  input  b,
  input  [1:0] Cin,
  output [1:0] Cout
);

  wire and_1_out, and_2_out, and_3_out, and_4_out, not_1_out, not_2_out, not_3_out, not_4_out;

  not not_1 (not_1_out, b);
  not not_2 (not_2_out, a);
  not not_3 (not_3_out, and_1_out);
  and and_1 (and_1_out, a, not_1_out);
  and and_2 (and_2_out, not_2_out, b);
  not not_4 (not_4_out, and_2_out);
  and and_3 (and_3_out, not_3_out, Cin[0]);
  and and_4 (and_4_out, Cin[1], not_4_out);
  or or_1 (Cout[0], and_3_out, and_2_out);
  or or_2 (Cout[1], and_1_out, and_4_out);
endmodule

module Comp4nat (
  input  [3:0] A,
  input  [3:0] B,
  output A_B,
  output A_B_2,
  output A_B_3
);

  wire not_1_out, not_2_out;
  wire [1:0] bit0_cout, bit1_cout, bit2_cout, bit3_cout;

  Comp1bit bit3 (.a(A[3]), .b(B[3]), .Cin(bit2_cout), .Cout(bit3_cout));
  Comp1bit bit2 (.a(A[2]), .b(B[2]), .Cin(bit1_cout), .Cout(bit2_cout));
  Comp1bit bit1 (.a(A[1]), .b(B[1]), .Cin(bit0_cout), .Cout(bit1_cout));
  not not_1 (not_1_out, bit3_cout[1]);
  not not_2 (not_2_out, bit3_cout[0]);
  Comp1bit bit0 (.a(A[0]), .b(B[0]), .Cin(2'b00), .Cout(bit0_cout));
  and and_1 (A_B_3, not_2_out, bit3_cout[1]);
  and and_2 (A_B, bit3_cout[0], not_1_out);
  xnor xnor_1 (A_B_2, bit3_cout[0], bit3_cout[1]);
endmodule

module Comp4ent (
  input  [3:0] A,
  input  [3:0] B,
  output A_B,
  output A_B_2,
  output A_B_3
);

  wire not_1_out, not_2_out;
  wire [1:0] bit0_cout, bit1_cout, bit2_cout, bit3_cout;

  Comp1bit bit3 (.a(B[3]), .b(A[3]), .Cin(bit2_cout), .Cout(bit3_cout));
  Comp1bit bit2 (.a(A[2]), .b(B[2]), .Cin(bit1_cout), .Cout(bit2_cout));
  Comp1bit bit1 (.a(A[1]), .b(B[1]), .Cin(bit0_cout), .Cout(bit1_cout));
  not not_1 (not_1_out, bit3_cout[1]);
  not not_2 (not_2_out, bit3_cout[0]);
  Comp1bit bit0 (.a(A[0]), .b(B[0]), .Cin(2'b00), .Cout(bit0_cout));
  and and_1 (A_B, bit3_cout[0], not_1_out);
  xnor xnor_1 (A_B_2, bit3_cout[0], bit3_cout[1]);
  and and_2 (A_B_3, not_2_out, bit3_cout[1]);

  // Notes on the sheet:
  //   Sa
  //   Sb
endmodule
