// Logisim project 3.2_BancRegsBiport+PC.circ as structural Verilog: 6 circuits, main circuit main
module main (
  input  Load,
  input  Increment,
  input  Write
);

  wire Reset_2_out, Reset_3_out, Reset_out, Sincro_2_out, Sincro_out;
  wire [1:0] IN_out, out1_out, out2_out;
  wire [7:0] bancregistres4x8b_1_regout1, bancregistres4x8b_1_regout2, Data_IN_out, mult8bits_1_out_4,
       n1_out, n2_out, New_PC_value_out, pc8bits_1_pcout;

  Button Sincro (.out(Sincro_out));
  Button Reset (.out(Reset_out));
  Slider #(.value('hc4)) Data_IN (.out(Data_IN_out));
  Slider #(.width(2), .value('h3)) IN (.out(IN_out));
  Slider #(.width(2), .value('h2)) out1 (.out(out1_out));
  Slider #(.width(2), .value('h3)) out2 (.out(out2_out));
  BancRegistres4x8b bancregistres4x8b_1 (
    .RegIn(Data_IN_out), .\NúmRegIn (IN_out), .Wr(Write), .Sinc(Sincro_out), .Reset(Reset_out),
    .RegOut1(bancregistres4x8b_1_regout1), .RegOut2(bancregistres4x8b_1_regout2), .\NúmRegOut2 (out2_out),
    .\NúmRegOut1 (out1_out));
  // Probe on bancregistres4x8b_1_regout2
  // Probe on bancregistres4x8b_1_regout1
  Button Sincro_2 (.out(Sincro_2_out));
  Slider #(.value('hf0)) New_PC_value (.out(New_PC_value_out));
  PC8bits pc8bits_1 (
    .NewPC(New_PC_value_out), .Sinc(Sincro_2_out), .Reset(Reset_2_out), .PCout(pc8bits_1_pcout),
    .Inc(Increment), .Load(Load));
  // Probe on pc8bits_1_pcout
  Button Reset_2 (.out(Reset_2_out));
  Slider #(.value('h1c)) n1 (.out(n1_out));
  Button Reset_3 (.out(Reset_3_out));
  Slider #(.value('h5)) n2 (.out(n2_out));
  Mult8Bits mult8bits_1 (.n1(n1_out), .n2(n2_out), .out_4(mult8bits_1_out_4), .RESET(Reset_3_out));
  // Probe on mult8bits_1_out_4

  // Notes on the sheet:
  //   PractFC3.2 Equip XI13$Eric García Castro$Iván Molinero Moreno
  //   EXTRA: Simulació de programa ARM:$Multiplicació emprant la suma
endmodule

module BancRegistres4x8b (
  input  [7:0] RegIn,
  input  Wr,
  input  Sinc,
  input  Reset,
  input  [1:0] \NúmRegIn ,
  input  [1:0] \NúmRegOut1 ,
  input  [1:0] \NúmRegOut2 ,
  output [7:0] RegOut1,
  output [7:0] RegOut2
);

  wire demultiplexer_1_out0, demultiplexer_1_out1, demultiplexer_1_out2, demultiplexer_1_out3;
  wire [7:0] R0_dout, R1_dout, R2_dout, R3_dout;

  Demultiplexer #(.select(2), .enable("false")) demultiplexer_1 (
    .out0(demultiplexer_1_out0), .out1(demultiplexer_1_out1), .out2(demultiplexer_1_out2),
    .out3(demultiplexer_1_out3), .in(Sinc), .sel(\NúmRegIn ));
  Registre8bits R0 (.Wr(Wr), .Sinc(demultiplexer_1_out0), .Reset(Reset), .Din(RegIn), .Dout(R0_dout));
  Registre8bits R1 (.Wr(Wr), .Sinc(demultiplexer_1_out1), .Reset(Reset), .Din(RegIn), .Dout(R1_dout));
  Registre8bits R2 (.Wr(Wr), .Sinc(demultiplexer_1_out2), .Reset(Reset), .Din(RegIn), .Dout(R2_dout));
  Registre8bits R3 (.Wr(Wr), .Sinc(demultiplexer_1_out3), .Reset(Reset), .Din(RegIn), .Dout(R3_dout));
  Multiplexer #(.select(2), .width(8), .enable("false")) multiplexer_1 (
    .in0(R0_dout), .in1(R1_dout), .in2(R2_dout), .in3(R3_dout), .out(RegOut1), .sel(\NúmRegOut1 ));
  Multiplexer #(.select(2), .width(8), .enable("false")) multiplexer_2 (
    .in0(R0_dout), .in1(R1_dout), .in2(R2_dout), .in3(R3_dout), .out(RegOut2), .sel(\NúmRegOut2 ));
endmodule

module PC8bits (
  input  [7:0] NewPC,
  input  Inc,
  input  Reset,
  input  Load,
  input  Sinc,
  output [7:0] PCout
);

  wire xor_1_out;
  wire [7:0] adder_1_out, multiplexer_1_out;

  Adder adder_1 (.a(8'h1), .b(PCout), .out(adder_1_out));  // open: cin, cout
  xor xor_1 (xor_1_out, Inc, Load);
  Multiplexer #(.width(8), .enable("false")) multiplexer_1 (
    .in0(adder_1_out), .in1(NewPC), .out(multiplexer_1_out), .sel(Load));
  Registre8bits PC___R15 (.Wr(xor_1_out), .Sinc(Sinc), .Reset(Reset), .Din(multiplexer_1_out), .Dout(PCout));
endmodule

module Registre8bits (
  input  [7:0] Din,
  input  Wr,
  input  Sinc,
  input  Reset,
  output [7:0] Dout
);

  Register #(.Select("low")) Reg8b (.D(Din), .en(Wr), .Q(Dout), .clk(Sinc), .clr(Reset));
endmodule

module Comp8 (
  input  [7:0] A,
  input  [7:0] B,
  output A___B,
  output A___B_2,
  output A___B_3
);

  wire and_2_out, and_3_out, comp4ent_1_a_b, comp4ent_1_a_b_2, comp4ent_1_a_b_3, comp4nat_1_a_b,
       comp4nat_1_a_b_2, comp4nat_1_a_b_3;

  or or_1 (A___B, comp4ent_1_a_b, and_2_out);
  Comp4ent comp4ent_1 (
    .A(A[7:4]), .B(B[7:4]), .A_B(comp4ent_1_a_b), .A_B_2(comp4ent_1_a_b_2), .A_B_3(comp4ent_1_a_b_3));
  Comp4nat comp4nat_1 (
    .A_B_3(comp4nat_1_a_b_3), .A_B_2(comp4nat_1_a_b_2), .A_B(comp4nat_1_a_b), .A(A[3:0]), .B(B[3:0]));
  and and_1 (A___B_2, comp4ent_1_a_b_2, comp4nat_1_a_b_2);
  and and_2 (and_2_out, comp4ent_1_a_b_2, comp4nat_1_a_b);
  and and_3 (and_3_out, comp4ent_1_a_b_2, comp4nat_1_a_b_3);
  or or_2 (A___B_3, comp4ent_1_a_b_3, and_3_out);
endmodule

module Mult8Bits (
  input  [7:0] n1,
  input  [7:0] n2,
  input  RESET,
  output [7:0] out_4
);

  wire and_1_out, clock_1_out, clock_2_out, comp8_3_a___b_2, comp8_4_a___b_2, comp8_5_a___b_2,
       comp8_6_a___b_2, comp8_7_a___b_2, comp8_8_a___b, comp8_8_a___b_3, comp8_9_a___b_2, nor_1_out,
       nor_2_out, not_1_out, not_2_out, not_3_out, not_4_out, or_1_out, or_2_out, or_3_out, or_4_out,
       or_5_out, or_6_out;
  wire [1:0] bit_extender_1_out, comp8_1_a___b_2, multiplexer_2_out, multiplexer_3_out;
  wire [7:0] adder_1_out, adder_2_out, bancregistres4x8b_1_regout2, bitselector_1_out, bitselector_2_out,
       multiplexer_1_out, multiplexer_4_out, multiplexer_5_out, multiplexer_6_out, multiplexer_7_out,
       pc8bits_1_pcout;

  or or_1 (or_1_out, comp8_9_a___b_2, and_1_out);
  nor nor_1 (nor_1_out, and_1_out, comp8_9_a___b_2);
  not not_1 (not_1_out, clock_1_out);
  Clock clock_1 (.out(clock_1_out));
  and and_1 (and_1_out, comp8_7_a___b_2, or_2_out);
  Multiplexer #(.width(8), .disabled(0), .enable("false")) multiplexer_1 (
    .in0(8'h4), .in1(8'h7), .out(multiplexer_1_out), .sel(comp8_9_a___b_2));
  PC8bits pc8bits_1 (
    .NewPC(multiplexer_1_out), .Sinc(not_1_out), .Reset(RESET), .PCout(pc8bits_1_pcout), .Inc(nor_1_out),
    .Load(or_1_out));
  or or_2 (or_2_out, comp8_8_a___b, comp8_8_a___b_3);
  Comp8 comp8_1 (.A(pc8bits_1_pcout), .B({8{1'b0}}), .A___B_2(comp8_1_a___b_2[0]));  // open: A___B, A___B_3
  Comp8 comp8_2 (.A(pc8bits_1_pcout), .B(8'h1), .A___B_2(comp8_1_a___b_2[1]));  // open: A___B, A___B_3
  Comp8 comp8_3 (.A(pc8bits_1_pcout), .B(8'h2), .A___B_2(comp8_3_a___b_2));  // open: A___B, A___B_3
  Comp8 comp8_4 (.A(pc8bits_1_pcout), .B(8'h3), .A___B_2(comp8_4_a___b_2));  // open: A___B, A___B_3
  Comp8 comp8_5 (.A(pc8bits_1_pcout), .B(8'h4), .A___B_2(comp8_5_a___b_2));  // open: A___B, A___B_3
  Comp8 comp8_6 (.A(pc8bits_1_pcout), .B(8'h5), .A___B_2(comp8_6_a___b_2));  // open: A___B, A___B_3
  Comp8 comp8_7 (.A(pc8bits_1_pcout), .B(8'h6), .A___B_2(comp8_7_a___b_2));  // open: A___B, A___B_3
  Comp8 comp8_8 (
    .A(bancregistres4x8b_1_regout2), .B(out_4), .A___B(comp8_8_a___b), .A___B_3(comp8_8_a___b_3));  // open: A___B_2
  Comp8 comp8_9 (.A(pc8bits_1_pcout), .B(8'h7), .A___B_2(comp8_9_a___b_2));  // open: A___B, A___B_3
  not not_2 (not_2_out, comp8_6_a___b_2);
  or or_3 (or_3_out, comp8_1_a___b_2[0], comp8_1_a___b_2[1], comp8_3_a___b_2, comp8_6_a___b_2, comp8_5_a___b_2);
  or or_4 (or_4_out, comp8_3_a___b_2, comp8_4_a___b_2);
  Adder adder_1 (.a(bancregistres4x8b_1_regout2), .b(out_4), .out(adder_1_out));  // open: cin, cout
  BitSelector #(.group(8)) bitselector_1 (.in(adder_1_out), .out(bitselector_1_out), .sel(not_3_out));
  not not_3 (not_3_out, comp8_5_a___b_2);
  Adder adder_2 (.a(bancregistres4x8b_1_regout2), .b(8'h1), .out(adder_2_out));  // open: cin, cout
  BitSelector #(.group(8)) bitselector_2 (.in(adder_2_out), .out(bitselector_2_out), .sel(not_2_out));
  nor nor_2 (nor_2_out, comp8_6_a___b_2, comp8_7_a___b_2);
  Multiplexer #(.width(2), .disabled(0), .enable("false")) multiplexer_2 (
    .in0(comp8_1_a___b_2), .in1(2'b11), .out(multiplexer_2_out), .sel(or_6_out));
  or or_5 (or_5_out, or_3_out, comp8_6_a___b_2);
  assign bit_extender_1_out = {{1{1'b0}}, nor_2_out};  // Bit_Extender bit_extender_1
  or or_6 (or_6_out, comp8_4_a___b_2, comp8_5_a___b_2);
  not not_4 (not_4_out, comp8_1_a___b_2[0]);
  Clock clock_2 (.out(clock_2_out));
  Multiplexer #(.width(2), .disabled(0), .enable("false")) multiplexer_3 (
    .in0(2'b11), .in1(2'b10), .out(multiplexer_3_out), .sel(comp8_7_a___b_2));
  Multiplexer #(.width(8), .disabled(0), .enable("false")) multiplexer_4 (
    .in0(n1), .in1(n2), .out(multiplexer_4_out), .sel(not_4_out));
  Multiplexer #(.width(8), .disabled(0), .enable("false")) multiplexer_5 (
    .in0(bitselector_1_out), .in1(multiplexer_7_out), .out(multiplexer_5_out), .sel(not_3_out));
  Multiplexer #(.width(8), .disabled(0), .enable("false")) multiplexer_6 (
    .in0(multiplexer_5_out), .in1(bitselector_2_out), .out(multiplexer_6_out), .sel(comp8_6_a___b_2));
  BancRegistres4x8b bancregistres4x8b_1 (
    .RegIn(multiplexer_6_out), .\NúmRegIn (multiplexer_2_out), .Wr(or_5_out), .Sinc(clock_2_out),
    .Reset(RESET), .RegOut1(out_4), .RegOut2(bancregistres4x8b_1_regout2), .\NúmRegOut2 (bit_extender_1_out),
    .\NúmRegOut1 (multiplexer_3_out));
  Multiplexer #(.width(8), .disabled(0), .enable("false")) multiplexer_7 (
    .in0(multiplexer_4_out), .in1({8{1'b0}}), .out(multiplexer_7_out), .sel(or_4_out));
  // Probe on bancregistres4x8b_1_regout2

  // Notes on the sheet:
  //   EXTRA: Simulació de programa ARM:$Multiplicació emprant la suma
  //   beq 0x7
  //   bne #0x4
  //   bne #0x4
  //   beq 0x7
  //   add r3, r1
  //   add r0, #1
  //   cmp r0, r2
  //   mov r1, n1
  //   mov r2, n2
  //   mov r0,#0
  //   mov r3, #0
  //   x
  //   RESULT
endmodule
