// Logisim project 3.3_Comp4desc.circ as structural Verilog: 4 circuits, main circuit main
module main (
);

  Comp4nat comp4nat_1 ();  // open: A_B, A_B_2, A_B_3, A, B
  Comp1bitDesc comp1bitdesc_1 ();  // open: a, b, Cin, Cout
  Comp4ent comp4ent_1 ();  // open: A_B, A_B_2, A_B_3, A, B

  // Notes on the sheet:
  //   PractFC3.3 Equip AA99$NomA Cognom1A Cognom2A$NomB Cognom1B Cognom2B
endmodule

module Comp1bitDesc (
  input  a,
  input  b,
  input  [2:0] Cin,
  output [2:0] Cout
);
endmodule

module Comp4nat (
  input  [3:0] A,
  input  [3:0] B,
  output A_B,
  output A_B_2,
  output A_B_3
);

  wire [2:0] bit0_cout, bit1_cout, bit2_cout, bit3_cout, undriven;

  Comp1bitDesc bit3 (.a(A[3]), .b(B[3]), .Cin(undriven), .Cout(bit3_cout));
  Comp1bitDesc bit1 (.a(A[1]), .b(B[1]), .Cin(bit2_cout), .Cout(bit1_cout));
  Comp1bitDesc bit2 (.a(A[2]), .b(B[2]), .Cin(bit3_cout), .Cout(bit2_cout));
  Comp1bitDesc bit0 (.a(A[0]), .b(B[0]), .Cin(bit1_cout), .Cout(bit0_cout));
endmodule

module Comp4ent (
  input  [3:0] A,
  input  [3:0] B,
  output A_B,
  output A_B_2,
  output A_B_3
);

  wire [2:0] bit0_cout, bit1_cout, bit2_cout, bit3_cout, undriven;

  Comp1bitDesc bit3 (.Cin(undriven), .Cout(bit3_cout));  // open: a, b
  Comp1bitDesc bit2 (.a(A[2]), .b(B[2]), .Cin(bit3_cout), .Cout(bit2_cout));
  Comp1bitDesc bit1 (.a(A[1]), .b(B[1]), .Cin(bit2_cout), .Cout(bit1_cout));
  Comp1bitDesc bit0 (.a(A[0]), .b(B[0]), .Cin(bit1_cout), .Cout(bit0_cout));

  // Notes on the sheet:
  //   Sa
  //   Sb
endmodule
