// Logisim project 3.4_RegDespl.circ as structural Verilog: 19 circuits, main circuit main
module main (
);

  RegDespl regdespl_1 ();  // open: Load, SR, Op, nbits, sinc, entrada, sortida, reset

  // Notes on the sheet:
  //   PractFC3.4 Equip AA99$NomA Cognom1A Cognom2A$NomB Cognom1B Cognom2B
endmodule

// Reg. Despl
module RegDespl (
  input  [7:0] entrada,
  input  Load,
  input  SR,
  input  [1:0] Op,
  input  [2:0] nbits,
  input  sinc,
  input  reset,
  output [7:0] sortida
);

  Reg8bits reg8bits_1 (.Dout(sortida));  // open: Wr, Sinc, Reset, Din
  BarrelShifter barrelshifter_1 (.in(sortida));  // open: Op, nbits, out

  // Notes on the sheet:
  //   00 LSL$01 LSR$10 ASR$11 ROR
endmodule

module LSL1 (
  input  [7:0] in,
  output [7:0] out
);
endmodule

module LSR1 (
  input  [7:0] in,
  output [7:0] out
);
endmodule

module ASR1 (
  input  [7:0] in,
  output [7:0] out
);
endmodule

module ROR1 (
  input  [7:0] in,
  output [7:0] out
);
endmodule

module LSL2 (
  input  [7:0] in,
  output [7:0] out
);
endmodule

module LSR2 (
  input  [7:0] in,
  output [7:0] out
);
endmodule

module ASR2 (
  input  [7:0] in,
  output [7:0] out
);
endmodule

module ROR2 (
  input  [7:0] in,
  output [7:0] out
);
endmodule

module LSL4 (
  input  [7:0] in,
  output [7:0] out
);
endmodule

module LSR4 (
  input  [7:0] in,
  output [7:0] out
);
endmodule

module ASR4 (
  input  [7:0] in,
  output [7:0] out
);
endmodule

module ROR4 (
  input  [7:0] in,
  output [7:0] out
);
endmodule

module SR1 (
  input  [7:0] in,
  input  [1:0] Op,
  input  SR,
  output [7:0] out
);

  LSL1 lsl1_1 ();  // open: in, out
  LSR1 lsr1_1 ();  // open: in, out
  ASR1 asr1_1 ();  // open: in, out
  ROR1 ror1_1 ();  // open: in, out

  // Notes on the sheet:
  //   00 LSL$01 LSR$10 ASR$11 ROR
endmodule

module SR2 (
  input  [7:0] in,
  input  [1:0] Op,
  input  SR,
  output [7:0] out
);

  LSL2 lsl2_1 ();  // open: in, out
  LSR2 lsr2_1 ();  // open: in, out
  ASR2 asr2_1 ();  // open: in, out
  ROR2 ror2_1 ();  // open: in, out

  // Notes on the sheet:
  //   00 LSL$01 LSR$10 ASR$11 ROR
endmodule

module SR4 (
  input  [7:0] in,
  input  [1:0] Op,
  input  SR,
  output [7:0] out
);

  LSR4 lsr4_1 ();  // open: in, out
  LSL4 lsl4_1 ();  // open: in, out
  ASR4 asr4_1 ();  // open: in, out
  ROR4 ror4_1 ();  // open: in, out

  // Notes on the sheet:
  //   00 LSL$01 LSR$10 ASR$11 ROR
endmodule

// Barrel Shifter
module BarrelShifter (
  input  [7:0] in,
  input  [1:0] Op,
  input  [2:0] nbits,
  output [7:0] out
);

  SR1 sr1_1 (.SR(nbits[0]));  // open: Op, in, out
  SR2 sr2_1 (.SR(nbits[1]));  // open: Op, in, out
  SR4 sr4_1 (.SR(nbits[2]));  // open: Op, in, out

  // Notes on the sheet:
  //   00 LSL$01 LSR$10 ASR$11 ROR
endmodule

module Reg8bits (
  input  [7:0] Din,
  input  Wr,
  input  Sinc,
  input  Reset,
  output [7:0] Dout
);

  Register #(.Select("low")) Reg8b (.D(Din), .en(Wr), .Q(Dout), .clk(Sinc), .clr(Reset));
endmodule
